# Fritzing sketch alu_v2 (saved by Fritzing 0.9.3b)
stripboards: 1

parts:
  IC1 = IC, DIP package, 20 pins [chip_label="Transceiver (245)"]  # not connected
  J1 = female pin header, 2 pins [form="♀ (female)"]  # not connected
  J2 = female pin header, 2 pins [form="♀ (female)"]  # not connected
  J3 = female pin header, 2 pins [form="♀ (female)"]  # not connected
  J4 = female pin header, 2 pins [form="♀ (female)"]  # not connected
  IC3 = IC, DIP package, 16 pins [chip_label="4-bit adder (283)"]
  J5 = female pin header, 2 pins [form="♀ (female)"]  # not connected
  J6 = female pin header, 2 pins [form="♀ (female)"]  # not connected
  J7 = female pin header, 2 pins [form="♀ (female)"]  # not connected
  J8 = female pin header, 2 pins [form="♀ (female)"]  # not connected
  IC2 = IC, DIP package, 16 pins [chip_label="4-bit adder (283)"]
  IC4 = IC, DIP package, 14 pins [chip_label="XOR (86)"]
  J9 = female pin header, 2 pins [form="♀ (female)"]
  J10 = female pin header, 2 pins [form="♀ (female)"]
  J11 = female pin header, 2 pins [form="♀ (female)"]
  J12 = female pin header, 2 pins [form="♀ (female)"]
  J13 = female pin header, 2 pins [form="♀ (female)"]
  J14 = female pin header, 2 pins [form="♀ (female)"]
  J15 = female pin header, 2 pins [form="♀ (female)"]
  J16 = female pin header, 2 pins [form="♀ (female)"]
  IC5 = IC, DIP package, 14 pins [chip_label="XOR (86)"]
  J17 = female pin header, 1 pin [form="♀ (female)"]
  J18 = female pin header, 1 pin [form="♀ (female)"]
  J19 = female pin header, 1 pin [form="♀ (female)"]
  J20 = female pin header, 1 pin [form="♀ (female)"]
  J21 = female pin header, 1 pin [form="♀ (female)"]
  J22 = female pin header, 1 pin [form="♀ (female)"]
  J23 = female pin header, 1 pin [form="♀ (female)"]
  J24 = female pin header, 1 pin [form="♀ (female)"]
  J25 = female pin header, 1 pin [form="♀ (female)"]
  J26 = female pin header, 1 pin [form="♀ (female)"]
  J27 = female pin header, 1 pin [form="♀ (female)"]

nets:
  N1: IC3.pin1, J21.pin1
  N2: IC3.pin2, IC5.pin11
  N3: IC3.pin3, J10.pin1
  N4: IC3.pin4, J22.pin1
  N5: IC3.pin5, J10.pin2
  N6: IC3.pin6, IC5.pin8
  N7: IC3.pin7, IC4.pin2, IC4.pin5, IC4.pin10, IC4.pin13, IC5.pin2, IC5.pin5, IC5.pin10, IC5.pin13, J27.pin1
  N8: IC3.pin8, IC2.pin8, IC4.pin7, IC5.pin7, J26.pin1
  N9: IC3.pin9, IC2.pin7
  N10: IC3.pin10, J23.pin1
  N11: IC3.pin11, J9.pin1
  N12: IC3.pin12, IC5.pin3
  N13: IC3.pin13, J24.pin1
  N14: IC3.pin14, J9.pin2
  N15: IC3.pin15, IC5.pin6
  N16: IC3.pin16, IC2.pin16, IC4.pin14, IC5.pin14
  N17: IC2.pin1, J20.pin1
  N18: IC2.pin2, J11.pin1
  N19: IC2.pin3, IC4.pin11
  N20: IC2.pin4, J19.pin1
  N21: IC2.pin5, J11.pin2
  N22: IC2.pin6, IC4.pin8
  N23: IC2.pin9, J25.pin1
  N24: IC2.pin10, J18.pin1
  N25: IC2.pin11, IC4.pin3
  N26: IC2.pin12, J12.pin1
  N27: IC2.pin13, J17.pin1
  N28: IC2.pin14, J12.pin2
  N29: IC2.pin15, IC4.pin6
  N30: IC4.pin1, J16.pin1
  N31: IC4.pin4, J16.pin2
  N32: IC4.pin9, J15.pin2
  N33: IC4.pin12, J15.pin1
  N34: J13.pin1, IC5.pin1
  N35: J13.pin2, IC5.pin4
  N36: J14.pin1, IC5.pin12
  N37: J14.pin2, IC5.pin9

notes:
  0V
  +ve
  To Flags
  To bus
  Subtract
  B in
  A in
