# Fritzing sketch clock (saved by Fritzing 0.9.3b)
stripboards: 1

parts:
  J24 = female pin header, 1 pin [form="♀ (female)"]
  LED2 = LED - 5mm [color="Blue (470nm)" package="5 mm [THT]"]
  J30 = female pin header, 1 pin [form="♀ (female)"]
  J31 = female pin header, 1 pin [form="♀ (female)"]
  IC4 = IC, DIP package, 8 pins [chip_label=555]
  IC6 = IC, DIP package, 8 pins [chip_label=555]
  IC7 = IC, DIP package, 8 pins [chip_label=555]
  J34 = female pin header, 1 pin [form="♀ (female)"]
  IC8 = IC, DIP package, 14 pins [chip_label="NOT (04)"]
  IC9 = IC, DIP package, 14 pins [chip_label="2in OR (32)"]
  S1 = Pushbutton [package="[THT]"]
  C3 = Ceramic Capacitor [capacitance=10nF package="100 mil [THT, multilayer]"]
  C2 = Ceramic Capacitor [capacitance=100nF package="100 mil [THT, multilayer]"]
  R2 = Resistor [tolerance=±5% resistance=1k package=THT]
  R3 = Trimmer Potentiometer [maximum_resistance=10kΩ package=THT]
  R4 = Resistor [tolerance=±5% resistance=1k package=THT]
  C4 = Ceramic Capacitor [capacitance=1µF package="100 mil [THT, multilayer]"]
  R1 = Resistor [tolerance=±5% resistance=1M package=THT]
  R5 = Resistor [tolerance=±5% resistance=1k package=THT]
  C5 = Ceramic Capacitor [capacitance=10nF package="100 mil [THT, multilayer]"]
  R6 = Resistor [tolerance=±5% resistance=1k package=THT]
  R7 = Resistor [tolerance=±5% resistance=1k package=THT]
  S2 = Toggle Switch [package=THT]
  IC5 = IC, DIP package, 14 pins [chip_label="2in AND (08)"]
  J35 = female pin header, 1 pin [form="♀ (female)"]
  R8 = Resistor [tolerance=±5% resistance=220 package=THT]
  C6 = Ceramic Capacitor [capacitance=10nF package="100 mil [THT, multilayer]"]

nets:
  N1: J24.pin1, IC4.pin1, IC4.pin6, IC6.pin1, IC7.pin1, IC8.pin7, IC9.pin7, S1.Pin_3, S1.Pin_4, C3.0, C2.0, C4.1, C5.1, S2.COM, IC5.pin7, R8.Pin_1, C6.0
  N2: LED2.cathode, J30.pin1, IC8.pin3, IC5.pin6
  N3: J31.pin1, IC8.pin1
  N4: IC4.pin2, R6.Pin_1, S2.L1
  N5: IC4.pin3, IC8.pin13, IC5.pin9
  N6: IC4.pin4, R7.Pin_1, S2.L2
  N7: IC4.pin5, C5.0
  N8: IC4.pin8, IC6.pin4, IC6.pin8, IC7.pin4, IC7.pin8, J34.pin1, IC8.pin14, IC9.pin14, R4.Pin_0, R1.Pin_0, R5.Pin_0, R6.Pin_0, R7.Pin_0, IC5.pin14
  N9: IC6.pin2, IC6.pin6, R3.wiper, C4.0
  N10: IC6.pin3, IC5.pin10
  N11: IC6.pin5, C6.1
  N12: IC6.pin7, R2.Pin_0, R4.Pin_1
  N13: IC7.pin2, S1.Pin_1, S1.Pin_2, R5.Pin_1
  N14: IC7.pin3, IC5.pin13
  N15: IC7.pin5, C3.1
  N16: IC7.pin6, IC7.pin7, C2.1, R1.Pin_1
  N17: IC8.pin2, IC5.pin5
  N18: IC8.pin4, J35.pin1
  N19: IC8.pin12, IC5.pin12
  N20: IC9.pin4, IC9.pin11, IC5.pin4, R8.Pin_0
  N21: IC9.pin12, IC5.pin11
  N22: IC9.pin13, IC5.pin8
  N23: R2.Pin_1, R3.leg1

notes:
  0V
  +ve
  To bus
  Clock
  Halt
  +V 0V
  Confirm R and C values.
  !Clock
