# Fritzing sketch eeprom_programmer_v2 (saved by Fritzing 0.9.4)
stripboards: 1

parts:
  IC1 = IC, DIP package, 24 pins [chip_label=M28C16]
  IC2 = IC, DIP package, 30 pins [chip_label="Arduino Nano"]
  IC3 = IC, DIP package, 16 pins [chip_label="HC595 (8bit shift reg)"]
  IC4 = IC, DIP package, 16 pins [chip_label="HC595 (8bit shift reg)"]

nets:
  N1: IC1.pin1, IC4.pin4
  N2: IC1.pin2, IC4.pin3
  N3: IC1.pin3, IC4.pin2
  N4: IC1.pin4, IC4.pin1
  N5: IC1.pin5, IC3.pin7
  N6: IC1.pin6, IC3.pin6
  N7: IC1.pin7, IC3.pin5
  N8: IC1.pin8, IC3.pin4
  N9: IC1.pin9, IC3.pin3
  N10: IC1.pin10, IC3.pin2
  N11: IC1.pin11, IC3.pin1
  N12: IC1.pin12, IC1.pin18, IC2.pin19, IC3.pin8, IC3.pin13, IC4.pin8, IC4.pin13
  N13: IC1.pin13, IC2.pin30
  N14: IC1.pin14, IC2.pin29
  N15: IC1.pin15, IC2.pin28
  N16: IC1.pin16, IC2.pin27
  N17: IC1.pin17, IC2.pin26
  N18: IC1.pin19, IC2.pin24
  N19: IC1.pin20, IC2.pin23
  N20: IC1.pin21, IC2.pin22
  N21: IC1.pin22, IC2.pin21
  N22: IC1.pin23, IC4.pin5
  N23: IC1.pin24, IC2.pin12, IC3.pin10, IC3.pin16, IC4.pin10, IC4.pin16
  N24: IC2.pin1, IC3.pin12, IC4.pin12
  N25: IC2.pin20, IC4.pin14
  N26: IC2.pin25, IC3.pin11, IC4.pin11
  N27: IC3.pin14, IC4.pin9

notes:
  0V
  +ve
