# Fritzing sketch ir (saved by Fritzing 0.9.5d)
stripboards: 1

parts:
  LED1 = LED - 3mm [color="Red (633nm)" package="3 mm [THT]"]
  LED2 = LED - 3mm [color="Red (633nm)" package="3 mm [THT]"]
  LED3 = LED - 3mm [color="Red (633nm)" package="3 mm [THT]"]
  LED4 = LED - 3mm [color="Red (633nm)" package="3 mm [THT]"]
  LED5 = LED - 3mm [color="Red (633nm)" package="3 mm [THT]"]
  LED6 = LED - 3mm [color="Red (633nm)" package="3 mm [THT]"]
  LED7 = LED - 3mm [color="Red (633nm)" package="3 mm [THT]"]
  LED8 = LED - 3mm [color="Red (633nm)" package="3 mm [THT]"]
  J1 = female pin header, 2 pins [form="♀ (female)"]
  J2 = female pin header, 2 pins [form="♀ (female)"]
  J3 = female pin header, 2 pins [form="♀ (female)"]
  J4 = female pin header, 2 pins [form="♀ (female)"]
  IC2 = IC, DIP package, 16 pins [chip_label="4-bit reg"]
  IC3 = IC, DIP package, 16 pins [chip_label="4-bit reg"]
  J5 = female pin header, 2 pins [form="♀ (female)"]
  J6 = female pin header, 2 pins [form="♀ (female)"]
  J7 = female pin header, 2 pins [form="♀ (female)"]
  J8 = female pin header, 2 pins [form="♀ (female)"]
  R1 = Resistor [tolerance=±5% resistance=82 package=THT]
  R2 = Resistor [tolerance=±5% resistance=82 package=THT]
  R3 = Resistor [tolerance=±5% resistance=82 package=THT]
  R4 = Resistor [tolerance=±5% resistance=82 package=THT]
  R6 = Resistor [tolerance=±5% resistance=82 package=THT]
  R7 = Resistor [tolerance=±5% resistance=82 package=THT]
  R8 = Resistor [tolerance=±5% resistance=82 package=THT]
  R9 = Resistor [tolerance=±5% resistance=82 package=THT]

nets:
  N1: LED1.cathode, J1.pin1, IC3.pin3
  N2: LED1.anode, R9.Pin_1
  N3: LED2.cathode, J1.pin2, IC3.pin4
  N4: LED2.anode, R8.Pin_1
  N5: LED3.cathode, J2.pin1, IC3.pin5
  N6: LED3.anode, R7.Pin_1
  N7: LED4.cathode, J2.pin2, IC3.pin6
  N8: LED4.anode, R6.Pin_1
  N9: LED5.cathode, J3.pin1, IC2.pin3
  N10: LED5.anode, R4.Pin_0
  N11: LED6.cathode, J3.pin2, IC2.pin4
  N12: LED6.anode, R3.Pin_0
  N13: LED7.cathode, J4.pin1, IC2.pin5
  N14: LED7.anode, R2.Pin_0
  N15: LED8.cathode, J4.pin2, IC2.pin6
  N16: LED8.anode, R1.Pin_0
  N17: IC2.pin1, IC2.pin2, IC2.pin8, IC3.pin1, IC3.pin2, IC3.pin8, R1.Pin_1, R2.Pin_1, R3.Pin_1, R4.Pin_1, R6.Pin_0, R7.Pin_0, R8.Pin_0, R9.Pin_0
  N18: IC2.pin7, IC3.pin7
  N19: IC2.pin9, IC2.pin10, IC3.pin9, IC3.pin10
  N20: IC2.pin11, J7.pin2
  N21: IC2.pin12, J7.pin1
  N22: IC2.pin13, J8.pin2
  N23: IC2.pin14, J8.pin1
  N24: IC2.pin15, IC3.pin15
  N25: IC2.pin16, IC3.pin16
  N26: IC3.pin11, J6.pin2
  N27: IC3.pin12, J6.pin1
  N28: IC3.pin13, J5.pin2
  N29: IC3.pin14, J5.pin1

notes:
  0V
  +ve
  To microcontroller
  To bus
  Reset
  !Load
  Clock
