# Fritzing sketch ram (saved by Fritzing 0.9.3b)
stripboards: 1

parts:
  J1 = female pin header, 2 pins [form="♀ (female)"]
  J2 = female pin header, 2 pins [form="♀ (female)"]
  J3 = female pin header, 2 pins [form="♀ (female)"]
  J4 = female pin header, 2 pins [form="♀ (female)"]
  J5 = female pin header, 2 pins [form="♀ (female)"]
  J6 = female pin header, 2 pins [form="♀ (female)"]
  J7 = female pin header, 2 pins [form="♀ (female)"]
  J8 = female pin header, 2 pins [form="♀ (female)"]
  IC2 = IC, DIP package, 24 pins [chip_label="RAM (6116P)"]
  IC3 = IC, DIP package, 16 pins [chip_label="Mem Bank (74LS173)"]
  J11 = female pin header, 1 pin [form="♀ (female)"]
  J10 = female pin header, 3 pins [form="♀ (female)"]
  LED1 = LED - 5mm [color="Red (633nm)" package="5 mm [THT]"]
  LED2 = LED - 5mm [color="Red (633nm)" package="5 mm [THT]"]
  LED3 = LED - 5mm [color="Red (633nm)" package="5 mm [THT]"]

nets:
  N1: J1.pin1, IC2.pin1
  N2: J1.pin2, IC2.pin2
  N3: J2.pin1, IC2.pin3
  N4: J2.pin2, IC2.pin4
  N5: J3.pin1, IC2.pin5
  N6: J3.pin2, IC2.pin6
  N7: J4.pin1, IC2.pin7
  N8: J4.pin2, IC2.pin8
  N9: J5.pin1, IC2.pin17
  N10: J5.pin2, IC2.pin16
  N11: J6.pin1, IC2.pin15
  N12: J6.pin2, IC2.pin14
  N13: J7.pin1, IC2.pin10
  N14: J7.pin2, IC2.pin9
  N15: J8.pin1, IC2.pin13
  N16: J8.pin2, IC2.pin11
  N17: IC2.pin12, IC2.pin18, IC3.pin1, IC3.pin2, IC3.pin8, LED1.anode, LED2.anode, LED3.anode
  N18: IC2.pin19, IC3.pin5, LED3.cathode
  N19: IC2.pin22, IC3.pin4, LED2.cathode
  N20: IC2.pin23, IC3.pin3, LED1.cathode
  N21: IC2.pin24, IC3.pin11, IC3.pin16
  N22: IC3.pin9, IC3.pin10, J11.pin1
  N23: IC3.pin12, J10.pin3
  N24: IC3.pin13, J10.pin2
  N25: IC3.pin14, J10.pin1

notes:
  0V
  +ve
  To MAR
  To bus
  !OE
  !WE
  CLR
  Bank Select
  !SetBank
  CLK
