# Fritzing sketch register (saved by Fritzing 0.9.4)
stripboards: 1

parts:
  IC1 = IC, DIP package, 20 pins [chip_label=Transceiver]
  LED1 = LED - 3mm [color="Red (633nm)" package="3 mm [THT]"]
  LED2 = LED - 3mm [color="Red (633nm)" package="3 mm [THT]"]
  LED3 = LED - 3mm [color="Red (633nm)" package="3 mm [THT]"]
  LED4 = LED - 3mm [color="Red (633nm)" package="3 mm [THT]"]
  LED5 = LED - 3mm [color="Red (633nm)" package="3 mm [THT]"]
  LED6 = LED - 3mm [color="Red (633nm)" package="3 mm [THT]"]
  LED7 = LED - 3mm [color="Red (633nm)" package="3 mm [THT]"]
  LED8 = LED - 3mm [color="Red (633nm)" package="3 mm [THT]"]
  J1 = female pin header, 2 pins [form="♀ (female)"]
  J2 = female pin header, 2 pins [form="♀ (female)"]
  J3 = female pin header, 2 pins [form="♀ (female)"]
  J4 = female pin header, 2 pins [form="♀ (female)"]
  IC2 = IC, DIP package, 16 pins [chip_label="4-bit reg"]
  IC3 = IC, DIP package, 16 pins [chip_label="4-bit reg"]
  J5 = female pin header, 2 pins [form="♀ (female)"]
  J6 = female pin header, 2 pins [form="♀ (female)"]
  J7 = female pin header, 2 pins [form="♀ (female)"]
  J8 = female pin header, 2 pins [form="♀ (female)"]

nets:
  N1: IC1.pin1, IC1.pin20, LED1.anode, LED2.anode, LED3.anode, LED4.anode, IC2.pin16, IC3.pin16
  N2: IC1.pin2, J1.pin1, IC3.pin3
  N3: IC1.pin3, LED1.cathode, J1.pin2, IC3.pin4
  N4: IC1.pin4, LED2.cathode, J2.pin1, IC3.pin5
  N5: IC1.pin5, LED3.cathode, J2.pin2, IC3.pin6
  N6: IC1.pin6, LED4.cathode, LED5.cathode, J3.pin1, IC2.pin3
  N7: IC1.pin7, LED6.cathode, J3.pin2, IC2.pin4
  N8: IC1.pin8, LED7.cathode, J4.pin1, IC2.pin5
  N9: IC1.pin9, LED8.cathode, J4.pin2, IC2.pin6
  N10: IC1.pin10, LED5.anode, LED6.anode, LED7.anode, LED8.anode, IC2.pin1, IC2.pin2, IC2.pin8, IC3.pin1, IC3.pin2, IC3.pin8
  N11: IC1.pin11, IC2.pin11, J7.pin2
  N12: IC1.pin12, IC2.pin12, J7.pin1
  N13: IC1.pin13, IC2.pin13, J8.pin2
  N14: IC1.pin14, IC2.pin14, J8.pin1
  N15: IC1.pin15, IC3.pin11, J6.pin2
  N16: IC1.pin16, IC3.pin12, J6.pin1
  N17: IC1.pin17, IC3.pin13, J5.pin2
  N18: IC1.pin18, IC3.pin14, J5.pin1
  N19: IC2.pin7, IC3.pin7
  N20: IC2.pin9, IC2.pin10, IC3.pin9, IC3.pin10
  N21: IC2.pin15, IC3.pin15

notes:
  0V
  +ve
  To ALU
  !Enable
  To bus
  Reset
  !Load
  Clock
