# Fritzing sketch rom (saved by Fritzing 0.9.4)
stripboards: 1

parts:
  J1 = female pin header, 2 pins [form="♀ (female)"]
  J2 = female pin header, 2 pins [form="♀ (female)"]
  J3 = female pin header, 2 pins [form="♀ (female)"]
  J4 = female pin header, 2 pins [form="♀ (female)"]
  J5 = female pin header, 2 pins [form="♀ (female)"]
  J6 = female pin header, 2 pins [form="♀ (female)"]
  J7 = female pin header, 2 pins [form="♀ (female)"]
  J8 = female pin header, 2 pins [form="♀ (female)"]
  IC2 = IC, DIP package, 24 pins [chip_label="ROM (28C16A)"]
  IC3 = IC, DIP package, 16 pins [chip_label="Rom Bank (74LS173)"]
  J11 = female pin header, 1 pin [form="♀ (female)"]
  LED1 = LED - 5mm [color="Red (633nm)" package="5 mm [THT]"]
  LED2 = LED - 5mm [color="Red (633nm)" package="5 mm [THT]"]
  LED3 = LED - 5mm [color="Red (633nm)" package="5 mm [THT]"]
  J12 = female pin header, 1 pin [form="♀ (female)"]
  J13 = female pin header, 1 pin [form="♀ (female)"]
  LS245_Transceiver = IC, DIP package, 20 pins [chip_label="LS245 Transceiver"]
  J14 = female pin header, 1 pin [form="♀ (female)"]
  LED4 = LED - 5mm [color="Red (633nm)" package="5 mm [THT]"]
  LED5 = LED - 5mm [color="Red (633nm)" package="5 mm [THT]"]
  LED6 = LED - 5mm [color="Red (633nm)" package="5 mm [THT]"]
  LED7 = LED - 5mm [color="Red (633nm)" package="5 mm [THT]"]
  LED8 = LED - 5mm [color="Red (633nm)" package="5 mm [THT]"]
  LED9 = LED - 5mm [color="Red (633nm)" package="5 mm [THT]"]
  LED10 = LED - 5mm [color="Red (633nm)" package="5 mm [THT]"]
  LED11 = LED - 5mm [color="Red (633nm)" package="5 mm [THT]"]

nets:
  N1: J1.pin1, IC2.pin1
  N2: J1.pin2, IC2.pin2
  N3: J2.pin1, IC2.pin3
  N4: J2.pin2, IC2.pin4
  N5: J3.pin1, IC2.pin5
  N6: J3.pin2, IC2.pin6
  N7: J4.pin1, IC2.pin7
  N8: J4.pin2, IC2.pin8
  N9: J5.pin1, LS245_Transceiver.pin18
  N10: J5.pin2, LS245_Transceiver.pin17
  N11: J6.pin1, LS245_Transceiver.pin16
  N12: J6.pin2, LS245_Transceiver.pin15
  N13: J7.pin1, IC3.pin13, LS245_Transceiver.pin12
  N14: J7.pin2, IC3.pin12, LS245_Transceiver.pin11
  N15: J8.pin1, LS245_Transceiver.pin14
  N16: J8.pin2, IC3.pin14, LS245_Transceiver.pin13
  N17: IC2.pin9, LS245_Transceiver.pin9, LED4.cathode
  N18: IC2.pin10, LS245_Transceiver.pin8, LED5.cathode
  N19: IC2.pin11, LS245_Transceiver.pin7, LED4.anode, LED5.anode, LED6.cathode
  N20: IC2.pin12, IC2.pin18, IC2.pin20, IC3.pin1, IC3.pin2, IC3.pin8, LED1.anode, LED2.anode, LED3.anode, LS245_Transceiver.pin10, LED10.anode, LED11.anode
  N21: IC2.pin13, LS245_Transceiver.pin6, LED7.cathode
  N22: IC2.pin14, LS245_Transceiver.pin5, LED6.anode, LED7.anode, LED8.cathode
  N23: IC2.pin15, LS245_Transceiver.pin4, LED9.cathode
  N24: IC2.pin16, LS245_Transceiver.pin3, LED8.anode, LED9.anode, LED10.cathode
  N25: IC2.pin17, LS245_Transceiver.pin2, LED11.cathode
  N26: IC2.pin19, IC3.pin3, LED1.cathode
  N27: IC2.pin21, IC2.pin24, IC3.pin11, IC3.pin16, J13.pin1, LS245_Transceiver.pin1, LS245_Transceiver.pin20
  N28: IC2.pin22, IC3.pin4, LED2.cathode
  N29: IC2.pin23, IC3.pin5, LED3.cathode
  N30: IC3.pin9, IC3.pin10, J11.pin1
  N31: IC3.pin15, J12.pin1
  N32: LS245_Transceiver.pin19, J14.pin1

notes:
  0V
  +ve
  To PC
  To bus
  !OE
  Reset
  !SetBank
  CLK
